// Logisim project 简易MIPS.circ as structural Verilog
module CPU (
);

  wire and_1_out, buffer_1_out, buffer_2_out, clk, not_1_out, or_1_out, or_2_out, or_3_out, or_4_out,
       \两数相等_1_x_y , \指令控制逻辑_1_beq , \指令控制逻辑_1_i_alu指令 , \指令控制逻辑_1_j , \指令控制逻辑_1_jr , \指令控制逻辑_1_lw ,
       \指令控制逻辑_1_sw , \指令控制逻辑_1_w_en , \指令控制逻辑_1_移位运算 ;
  wire [4:0] multiplexer_3_out, multiplexer_4_out, \指令拆分器_1__5_rd , \指令拆分器_1__5_rs , \指令拆分器_1__5_rt ,
       \指令拆分器_1__5_shamt ;
  wire [5:0] \指令拆分器_1__6_func , \指令拆分器_1__6_op , \指令控制逻辑_1_alu_op ;
  wire [25:0] \指令拆分器_1__26_addr ;
  wire [31:0] alu_1_out, bit_extender_1_out, bit_extender_2_out, multiplexer_1_out, multiplexer_2_out,
       multiplexer_5_out, multiplexer_6_out, multiplexer_7_out, multiplexer_8_out, \n32寄存器组_1_r1d ,
       \n32寄存器组_1_r2d , pc_1_pc, pc_1_pc_1, rom_1_data, \写入_out , \指令拆分器_1__32_imm , \读出_out ;

  PC pc_1 (.PC_IN(multiplexer_1_out), .PC_EN(or_1_out), .PC(pc_1_pc), .PC_1(pc_1_pc_1), .Clk(clk));
  Clock clock_1 (.out(clk));
  Multiplexer #(.width(32), .enable("false")) multiplexer_1 (
    .in0(multiplexer_2_out), .in1(bit_extender_1_out), .out(multiplexer_1_out), .sel(\指令控制逻辑_1_j ));
  or or_1 (or_1_out, \指令控制逻辑_1_j , \指令控制逻辑_1_jr , \两数相等_1_x_y );
  ROM #(.addrWidth(16), .dataWidth(32)) rom_1 (.addr(pc_1_pc[15:0]), .data(rom_1_data));  // open: sel
  assign bit_extender_1_out = {{6{\指令拆分器_1__26_addr [25]}}, \指令拆分器_1__26_addr };  // Bit_Extender bit_extender_1
  Multiplexer #(.width(32), .enable("false")) multiplexer_2 (
    .in0(\n32寄存器组_1_r1d ), .in1(alu_1_out), .out(multiplexer_2_out), .sel(\两数相等_1_x_y ));
  \指令拆分器  \u_指令拆分器_1  (
    .in_1(rom_1_data), ._6_func(\指令拆分器_1__6_func ), ._5_shamt(\指令拆分器_1__5_shamt ), ._5_rd(\指令拆分器_1__5_rd ),
    ._5_rt(\指令拆分器_1__5_rt ), ._5_rs(\指令拆分器_1__5_rs ), ._6_op(\指令拆分器_1__6_op ), ._32_imm(\指令拆分器_1__32_imm ),
    ._26_addr(\指令拆分器_1__26_addr ));
  Multiplexer #(.width(5), .enable("false")) multiplexer_3 (
    .in0(\指令拆分器_1__5_rd ), .in1(\指令拆分器_1__5_rt ), .out(multiplexer_3_out), .sel(or_2_out));
  assign bit_extender_2_out = {{27{1'b0}}, \指令拆分器_1__5_shamt };  // Bit_Extender bit_extender_2
  \指令控制逻辑  \u_指令控制逻辑_1  (
    .OP(\指令拆分器_1__6_op ), .Func(\指令拆分器_1__6_func ), .EN(clk), .ALU_OP(\指令控制逻辑_1_alu_op ),
    .W_EN(\指令控制逻辑_1_w_en ), .\移位运算 (\指令控制逻辑_1_移位运算 ), .jr(\指令控制逻辑_1_jr ), .\I_ALU指令 (\指令控制逻辑_1_i_alu指令 ),
    .lw(\指令控制逻辑_1_lw ), .sw(\指令控制逻辑_1_sw ), .beq(\指令控制逻辑_1_beq ), .j(\指令控制逻辑_1_j ));
  and and_1 (and_1_out, \指令控制逻辑_1_移位运算 , ~or_2_out);  // AND_Gate
  Multiplexer #(.width(5), .enable("false")) multiplexer_4 (
    .in0(\指令拆分器_1__5_rs ), .in1(\指令拆分器_1__5_rt ), .out(multiplexer_4_out), .sel(and_1_out));
  or or_2 (or_2_out, \指令控制逻辑_1_i_alu指令 , \指令控制逻辑_1_lw , \指令控制逻辑_1_sw );
  or or_3 (or_3_out, \指令控制逻辑_1_w_en , \指令控制逻辑_1_lw );
  Multiplexer #(.width(32), .enable("false")) multiplexer_5 (
    .in0(\n32寄存器组_1_r2d ), .in1(\指令拆分器_1__32_imm ), .out(multiplexer_5_out), .sel(or_2_out));
  \_32寄存器组  \u_32寄存器组_1  (
    .W_En(or_3_out), .W_star(multiplexer_3_out), .WD(multiplexer_8_out), .R1_star(multiplexer_4_out),
    .R2_star(\指令拆分器_1__5_rt ), .R1D(\n32寄存器组_1_r1d ), .R2D(\n32寄存器组_1_r2d ), .Clk(clk));
  \两数相等  \u_两数相等_1  (.X(\n32寄存器组_1_r1d ), .Y(\n32寄存器组_1_r2d ), .X_Y(\两数相等_1_x_y ), .\使能 (\指令控制逻辑_1_beq ));
  Multiplexer #(.width(32), .enable("false")) multiplexer_6 (
    .in0(\n32寄存器组_1_r1d ), .in1(pc_1_pc_1), .out(multiplexer_6_out), .sel(\两数相等_1_x_y ));
  ALU alu_1 (.ALU_OP(\指令控制逻辑_1_alu_op ), .X(multiplexer_6_out), .Y(multiplexer_7_out), .OUT(alu_1_out));
  Multiplexer #(.width(32), .enable("false")) multiplexer_7 (
    .in0(multiplexer_5_out), .in1(bit_extender_2_out), .out(multiplexer_7_out), .sel(\指令控制逻辑_1_移位运算 ));
  Multiplexer #(.width(32), .enable("false")) multiplexer_8 (
    .in0(alu_1_out), .in1(\读出_out ), .out(multiplexer_8_out), .sel(\指令控制逻辑_1_lw ));
  or or_4 (or_4_out, \指令控制逻辑_1_lw , \指令控制逻辑_1_sw );
  not not_1 (not_1_out, clk);
  buf buffer_1 (buffer_1_out, or_4_out);
  buf buffer_2 (buffer_2_out, buffer_1_out);
  assign \写入_out  = \指令控制逻辑_1_sw  ? \n32寄存器组_1_r2d  : 32'bz;  // Controlled_Buffer 写入
  assign \读出_out  = \指令控制逻辑_1_lw  ? \写入_out  : 32'bz;  // Controlled_Buffer 读出
  RAM #(.addrWidth(16), .dataWidth(32)) ram_1 (
    .addr(alu_1_out[15:0]), .data(\写入_out ), .sel(buffer_2_out), .clk(not_1_out), .ld(\指令控制逻辑_1_lw ));  // open: clr
  Pull_Resistor pull_resistor_1 (.node(\写入_out ));

  // Notes on the sheet:
  //   contents of rom_1 (hex, n*v repeats v):
  //   4080008 44080001 4080003 44080002 4080005 44080003 4080007 44080004 4080002 44080005 40100001
  //   40110002 40120003 40130004 40140005 4080005 40c0001 2745809 816c0003 2606801 2809801 1a0a001 2535809
  //   816c0003 2406801 2609001 1a09801 2325809 816c0003 2206801 2408801 1a09001 2115809 816c0003 2006801
  //   2208001 1a08801 9080001 250d0002 818d0001 84000011 44100001 44110002 44120003 44130004 44140005
endmodule

module \指令控制逻辑  (
  input  [5:0] OP,
  input  [5:0] Func,
  input  EN,
  output [5:0] ALU_OP,
  output W_EN,
  output \移位运算 ,
  output jr,
  output \I_ALU指令 ,
  output lw,
  output sw,
  output beq,
  output j
);

  wire and_1_out, and_2_out, and_3_out, beq_out, \I型指令_out , \i非alu指令_1_beq , \i非alu指令_1_lw , \i非alu指令_1_sw ,
       J_out, jr_out, nand_1_out, or_1_out, or_3_out, \R型指令_out , \进行移位运算_1_移位 ;
  wire [5:0] multiplexer_1_out, multiplexer_2_out;

  nor \R型指令  (\R型指令_out , OP[0], OP[1], OP[2], OP[4], OP[5], OP[3]);
  and u_J (J_out, OP[0], ~OP[1], ~OP[2], ~OP[3], ~OP[4], OP[5]);  // AND_Gate
  and u_beq (beq_out, ~OP[0], ~OP[1], ~OP[2], ~OP[3], ~OP[4], OP[5]);  // AND_Gate
  nor \I型指令  (\I型指令_out , \R型指令_out , J_out);
  nand nand_1 (nand_1_out, OP[4], OP[5]);
  or or_1 (or_1_out, \R型指令_out , \I型指令_out );
  Multiplexer #(.width(6), .enable("false")) multiplexer_1 (
    .in0(Func), .in1(OP), .out(multiplexer_1_out), .sel(\I型指令_out ));
  and and_1 (and_1_out, EN, or_1_out, nand_1_out);
  Multiplexer #(.width(6), .enable("false")) multiplexer_2 (
    .in0(multiplexer_1_out), .in1(6'b000001), .out(multiplexer_2_out), .sel(or_3_out));
  assign ALU_OP = and_1_out ? multiplexer_2_out : 6'bz;  // Controlled_Buffer controlled_buffer_1
  Pull_Resistor pull_resistor_1 (.node(ALU_OP));
  \进行移位运算  \u_进行移位运算_1  (.IN(Func), .\移位 (\进行移位运算_1_移位 ));
  and and_2 (and_2_out, and_1_out, ~or_3_out);  // AND_Gate
  or or_2 (W_EN, and_2_out, \移位运算 );
  and u_jr (jr_out, ~Func[0], ~Func[1], ~Func[2], ~Func[3], Func[4], ~Func[5]);  // AND_Gate
  and and_3 (and_3_out, \R型指令_out , jr_out);
  and and_4 (\移位运算 , \进行移位运算_1_移位 , \R型指令_out , EN);
  and and_5 (jr, EN, \R型指令_out , and_3_out);
  and and_6 (\I_ALU指令 , EN, nand_1_out, \I型指令_out );
  and and_7 (lw, EN, \i非alu指令_1_lw );
  or or_3 (or_3_out, sw, lw, beq);
  \I非ALU指令  \i非alu指令_1  (.IN(OP), .lw(\i非alu指令_1_lw ), .sw(\i非alu指令_1_sw ), .beq(\i非alu指令_1_beq ), .\使能 (\I型指令_out ));
  and and_8 (sw, \i非alu指令_1_sw , EN);
  and and_9 (beq, \i非alu指令_1_beq , EN);
  and and_10 (j, EN, J_out);
endmodule

module \指令拆分器  (
  input  [31:0] in_1,
  output [5:0] _6_func,
  output [4:0] _5_shamt,
  output [4:0] _5_rd,
  output [4:0] _5_rt,
  output [4:0] _5_rs,
  output [5:0] _6_op,
  output [31:0] _32_imm,
  output [25:0] _26_addr
);

  assign _32_imm = {{16{in_1[15]}}, in_1[15:0]};  // Bit_Extender bit_extender_1

  assign _5_rd = in_1[15:11];
  assign _5_rs = in_1[25:21];
  assign _5_rt = in_1[20:16];
  assign _5_shamt = in_1[10:6];
  assign _6_func = in_1[5:0];
  assign _6_op = in_1[31:26];
  assign _26_addr = in_1[25:0];
endmodule

module PC (
  input  [31:0] PC_IN,
  input  PC_EN,
  input  Clk,
  output [31:0] PC,
  output [31:0] PC_1
);

  wire [31:0] multiplexer_1_out;

  Pull_Resistor pull_resistor_1 (.node(PC_EN));
  Multiplexer #(.width(32), .enable("false")) multiplexer_1 (
    .in0(PC_1), .in1(PC_IN), .out(multiplexer_1_out), .sel(PC_EN));
  Register #(.width(32), .trigger("falling")) register_1 (.D(multiplexer_1_out), .Q(PC), .clk(Clk));  // open: en, clr
  \_32位全加器  \u_32位全加器_1  (.X(PC), .Cn_1(1'b0), .Y(32'h1), .OUT(PC_1));  // open: Cn_1_2

  // Notes on the sheet:
  //   PC_EN: pull=down
endmodule

module ALU (
  input  [5:0] ALU_OP,
  input  [31:0] X,
  input  [31:0] Y,
  output [31:0] OUT
);

  wire \alu指令选择器_1_add , \alu指令选择器_1_and , \alu指令选择器_1_jr , \alu指令选择器_1_or , \alu指令选择器_1_sll ,
       \alu指令选择器_1_slt , \alu指令选择器_1_sra , \alu指令选择器_1_srl , \alu指令选择器_1_sub , \alu指令选择器_1_xor ,
       multiplexer_2_out, or_1_out, or_3_out, \获取符号位_1_符号位 ;
  wire [31:0] and_1_out, bit_extender_1_out, multiplexer_1_out, \n32位全加器_1_out , not_1_out, or_2_out,
       shifter_1_out, shifter_2_out, shifter_3_out, xor_1_out;

  \ALU指令选择器  \alu指令选择器_1  (
    .ALU_OP(ALU_OP), .add(\alu指令选择器_1_add ), .sub(\alu指令选择器_1_sub ), .\and (\alu指令选择器_1_and ),
    .\or (\alu指令选择器_1_or ), .\xor (\alu指令选择器_1_xor ), .slt(\alu指令选择器_1_slt ), .sll(\alu指令选择器_1_sll ),
    .srl(\alu指令选择器_1_srl ), .sra(\alu指令选择器_1_sra ), .jr(\alu指令选择器_1_jr ));
  or or_1 (or_1_out, \alu指令选择器_1_sub , \alu指令选择器_1_slt );
  assign not_1_out = ~Y;  // NOT_Gate not_1, 32 bits wide
  Multiplexer #(.width(32), .enable("false")) multiplexer_1 (
    .in0(Y), .in1(not_1_out), .out(multiplexer_1_out), .sel(or_1_out));
  Multiplexer #(.enable("false")) multiplexer_2 (.in0(1'b0), .in1(1'b1), .out(multiplexer_2_out), .sel(or_1_out));
  assign and_1_out = Y & X;  // AND_Gate and_1, 32 bits wide
  assign or_2_out = Y | X;  // OR_Gate or_2, 32 bits wide
  assign xor_1_out = Y ^ X;  // XOR_Gate xor_1, 32 bits wide
  \_32位全加器  \u_32位全加器_1  (
    .X(X), .Cn_1(multiplexer_2_out), .Y(multiplexer_1_out), .OUT(\n32位全加器_1_out ));  // open: Cn_1_2
  \获取符号位  \u_获取符号位_1  (.IN(\n32位全加器_1_out ), .\符号位 (\获取符号位_1_符号位 ));
  assign OUT = \alu指令选择器_1_and  ? and_1_out : 32'bz;  // Controlled_Buffer controlled_buffer_1
  assign OUT = \alu指令选择器_1_or  ? or_2_out : 32'bz;  // Controlled_Buffer controlled_buffer_2
  assign OUT = \alu指令选择器_1_xor  ? xor_1_out : 32'bz;  // Controlled_Buffer controlled_buffer_3
  Shifter #(.width(32)) shifter_1 (.in(X), .\dist (Y[4:0]), .out(shifter_1_out));
  Shifter #(.width(32), .shift("lr")) shifter_2 (.in(X), .\dist (Y[4:0]), .out(shifter_2_out));
  Shifter #(.width(32), .shift("ar")) shifter_3 (.in(X), .\dist (Y[4:0]), .out(shifter_3_out));
  or or_3 (or_3_out, \alu指令选择器_1_sub , \alu指令选择器_1_add );
  assign OUT = or_3_out ? \n32位全加器_1_out  : 32'bz;  // Controlled_Buffer controlled_buffer_4
  assign bit_extender_1_out = {{31{1'b0}}, \获取符号位_1_符号位 };  // Bit_Extender bit_extender_1
  assign OUT = \alu指令选择器_1_sll  ? shifter_1_out : 32'bz;  // Controlled_Buffer controlled_buffer_5
  assign OUT = \alu指令选择器_1_srl  ? shifter_2_out : 32'bz;  // Controlled_Buffer controlled_buffer_6
  assign OUT = \alu指令选择器_1_sra  ? shifter_3_out : 32'bz;  // Controlled_Buffer controlled_buffer_7
  assign OUT = \alu指令选择器_1_jr  ? X : 32'bz;  // Controlled_Buffer controlled_buffer_8
  Pull_Resistor pull_resistor_1 (.node(OUT));
  assign OUT = \alu指令选择器_1_slt  ? bit_extender_1_out : 32'bz;  // Controlled_Buffer controlled_buffer_9

  // Other names for the same wires on the sheet: shamt[4:0] = Y[4:0]

  // Notes on the sheet:
  //   取低5位
endmodule

module \ALU指令选择器  (
  input  [5:0] ALU_OP,
  output add,
  output sub,
  output \and ,
  output \or ,
  output \xor ,
  output slt,
  output sll,
  output srl,
  output sra,
  output jr
);

  and and_1 (add, ALU_OP[0], ~ALU_OP[1], ~ALU_OP[2], ~ALU_OP[3], ~ALU_OP[4]);  // AND_Gate
  and and_2 (sub, ~ALU_OP[0], ALU_OP[1], ~ALU_OP[2], ~ALU_OP[3], ~ALU_OP[4]);  // AND_Gate
  and and_3 (\and , ALU_OP[0], ALU_OP[1], ~ALU_OP[2], ~ALU_OP[3], ~ALU_OP[4]);  // AND_Gate
  and and_4 (\or , ~ALU_OP[0], ~ALU_OP[1], ALU_OP[2], ~ALU_OP[3], ~ALU_OP[4]);  // AND_Gate
  and and_5 (\xor , ALU_OP[0], ~ALU_OP[1], ALU_OP[2], ~ALU_OP[3], ~ALU_OP[4]);  // AND_Gate
  and and_6 (slt, ALU_OP[0], ~ALU_OP[1], ~ALU_OP[2], ALU_OP[3], ~ALU_OP[4]);  // AND_Gate
  and and_7 (sll, ~ALU_OP[0], ALU_OP[1], ALU_OP[2], ~ALU_OP[3], ~ALU_OP[4]);  // AND_Gate
  and and_8 (srl, ALU_OP[0], ALU_OP[1], ALU_OP[2], ~ALU_OP[3], ~ALU_OP[4]);  // AND_Gate
  and and_9 (sra, ~ALU_OP[0], ~ALU_OP[1], ~ALU_OP[2], ALU_OP[3], ~ALU_OP[4]);  // AND_Gate
  and and_10 (jr, ~ALU_OP[0], ~ALU_OP[1], ~ALU_OP[2], ~ALU_OP[3], ALU_OP[4]);  // AND_Gate
endmodule

module \获取符号位  (
  input  [31:0] IN,
  output \符号位 
);


  assign \符号位  = IN[31];
endmodule

module \两数相等  (
  input  \使能 ,
  input  [31:0] X,
  input  [31:0] Y,
  output X_Y
);

  wire [3:0] and_1_out, and_2_out, and_3_out;
  wire [31:0] xnor_1_out;

  assign xnor_1_out = ~(X ^ Y);  // XNOR_Gate xnor_1, 32 bits wide
  assign and_1_out = xnor_1_out[23:20] & xnor_1_out[27:24] & xnor_1_out[31:28];  // AND_Gate and_1, 4 bits wide
  assign and_2_out = xnor_1_out[3:0] & xnor_1_out[7:4] & xnor_1_out[11:8] & xnor_1_out[15:12] & xnor_1_out[19:16];  // AND_Gate and_2, 4 bits wide
  assign and_3_out = and_2_out & and_1_out;  // AND_Gate and_3, 4 bits wide
  and and_4 (X_Y, \使能 , and_3_out[0], and_3_out[1], and_3_out[2], and_3_out[3]);
endmodule

module \J地址拼接  (
  input  [31:0] PC_4,
  input  [25:0] addr,
  output [31:0] Out
);


  assign Out = {PC_4[31:28], addr, 2'b00};
endmodule

module \_32位全加器  (
  input  [31:0] X,
  input  Cn_1,
  input  [31:0] Y,
  output Cn_1_2,
  output [31:0] OUT
);

  wire \八位全加器_1_cn_1_2 , \八位全加器_2_cn_1_2 , \八位全加器_3_cn_1_2 ;

  \八位全加器  \u_八位全加器_1  (.Cn_1(Cn_1), .X(X[7:0]), .Y(Y[7:0]), .OUT(OUT[7:0]), .Cn_1_2(\八位全加器_1_cn_1_2 ));
  \八位全加器  \u_八位全加器_2  (.Cn_1(\八位全加器_1_cn_1_2 ), .X(X[15:8]), .Y(Y[15:8]), .OUT(OUT[15:8]), .Cn_1_2(\八位全加器_2_cn_1_2 ));
  \八位全加器  \u_八位全加器_3  (
    .Cn_1(\八位全加器_2_cn_1_2 ), .X(X[23:16]), .Y(Y[23:16]), .OUT(OUT[23:16]), .Cn_1_2(\八位全加器_3_cn_1_2 ));
  \八位全加器  \u_八位全加器_4  (.Cn_1(\八位全加器_3_cn_1_2 ), .X(X[31:24]), .Y(Y[31:24]), .OUT(OUT[31:24]), .Cn_1_2(Cn_1_2));
endmodule

module \八位全加器  (
  input  [7:0] X,
  input  Cn_1,
  input  [7:0] Y,
  output Cn_1_2,
  output [7:0] OUT
);

  wire \一位全加器_1_c_1_2 , \一位全加器_2_c_1_2 , \一位全加器_3_c_1_2 , \一位全加器_4_c_1_2 , \一位全加器_5_c_1_2 , \一位全加器_6_c_1_2 ,
       \一位全加器_7_c_1_2 ;

  \一位全加器  \u_一位全加器_1  (.A(X[0]), .B(Y[0]), .C_1(Cn_1), .C(OUT[0]), .C_1_2(\一位全加器_1_c_1_2 ));
  \一位全加器  \u_一位全加器_2  (.A(X[1]), .B(Y[1]), .C_1(\一位全加器_1_c_1_2 ), .C(OUT[1]), .C_1_2(\一位全加器_2_c_1_2 ));
  \一位全加器  \u_一位全加器_3  (.A(X[2]), .B(Y[2]), .C_1(\一位全加器_2_c_1_2 ), .C(OUT[2]), .C_1_2(\一位全加器_3_c_1_2 ));
  \一位全加器  \u_一位全加器_4  (.A(X[3]), .B(Y[3]), .C_1(\一位全加器_3_c_1_2 ), .C(OUT[3]), .C_1_2(\一位全加器_4_c_1_2 ));
  \一位全加器  \u_一位全加器_5  (.A(X[4]), .B(Y[4]), .C_1(\一位全加器_4_c_1_2 ), .C(OUT[4]), .C_1_2(\一位全加器_5_c_1_2 ));
  \一位全加器  \u_一位全加器_6  (.A(X[5]), .B(Y[5]), .C_1(\一位全加器_5_c_1_2 ), .C(OUT[5]), .C_1_2(\一位全加器_6_c_1_2 ));
  \一位全加器  \u_一位全加器_7  (.A(X[6]), .B(Y[6]), .C_1(\一位全加器_6_c_1_2 ), .C(OUT[6]), .C_1_2(\一位全加器_7_c_1_2 ));
  \一位全加器  \u_一位全加器_8  (.A(X[7]), .B(Y[7]), .C_1(\一位全加器_7_c_1_2 ), .C(OUT[7]), .C_1_2(Cn_1_2));
endmodule

module \一位全加器  (
  input  A,
  input  B,
  input  C_1,
  output C,
  output C_1_2
);

  wire and_1_out, and_2_out, and_3_out, and_4_out, and_5_out, and_6_out, and_7_out, not_1_out, not_2_out,
       not_3_out, not_4_out, not_5_out, not_6_out;

  not not_1 (not_1_out, A);
  not not_2 (not_2_out, B);
  not not_3 (not_3_out, A);
  not not_4 (not_4_out, C_1);
  not not_5 (not_5_out, B);
  not not_6 (not_6_out, C_1);
  and and_1 (and_1_out, B, C_1);
  and and_2 (and_2_out, A, C_1);
  and and_3 (and_3_out, A, B);
  and and_4 (and_4_out, not_1_out, not_2_out, C_1);
  and and_5 (and_5_out, not_3_out, B, not_4_out);
  and and_6 (and_6_out, A, not_5_out, not_6_out);
  and and_7 (and_7_out, A, B, C_1);
  or or_1 (C_1_2, and_1_out, and_2_out, and_3_out);
  or or_2 (C, and_4_out, and_5_out, and_6_out, and_7_out);
endmodule

module \_32寄存器组  (
  input  W_En,
  input  [4:0] W_star,
  input  [31:0] WD,
  input  [4:0] R1_star,
  input  [4:0] R2_star,
  input  Clk,
  output [31:0] R1D,
  output [31:0] R2D
);

  wire and_1_out, and_2_out, and_3_out, and_4_out, decoder_2_out0, decoder_2_out1, decoder_2_out2,
       decoder_2_out3, decoder_3_out0, decoder_3_out1, decoder_3_out2, decoder_3_out3, W1, W2, W3, W4;
  wire [31:0] \n8_32寄存器组_0_1_r1_out , \n8_32寄存器组_0_1_r2_out , \n8_32寄存器组_1_1_r1_out , \n8_32寄存器组_1_1_r2_out ,
       \n8_32寄存器组_1_2_r1_out , \n8_32寄存器组_1_2_r2_out , \n8_32寄存器组_1_3_r1_out , \n8_32寄存器组_1_3_r2_out ;

  Decoder #(.select(2), .disabled(0), .enable("false")) decoder_1 (
    .out0(W1), .out1(W2), .out2(W3), .out3(W4), .sel(W_star[4:3]));
  Decoder #(.select(2), .disabled(0), .enable("false")) decoder_2 (
    .out0(decoder_2_out0), .out1(decoder_2_out1), .out2(decoder_2_out2), .out3(decoder_2_out3),
    .sel(R1_star[4:3]));
  Decoder #(.select(2), .disabled(0), .enable("false")) decoder_3 (
    .out0(decoder_3_out0), .out1(decoder_3_out1), .out2(decoder_3_out2), .out3(decoder_3_out3),
    .sel(R2_star[4:3]));
  and and_1 (and_1_out, W1, W_En);
  \_8_32寄存器组_0  \u_8_32寄存器组_0_1  (
    .R1_star(R1_star[2:0]), .W_En(and_1_out), .W_star(W_star[2:0]), .R2_star(R2_star[2:0]), .WD(WD),
    .R1_Out(\n8_32寄存器组_0_1_r1_out ), .R2_Out(\n8_32寄存器组_0_1_r2_out ), .Clk(Clk));
  and and_2 (and_2_out, W2, W_En);
  assign R1D = decoder_2_out0 ? \n8_32寄存器组_0_1_r1_out  : 32'bz;  // Controlled_Buffer controlled_buffer_1
  assign R2D = decoder_3_out0 ? \n8_32寄存器组_0_1_r2_out  : 32'bz;  // Controlled_Buffer controlled_buffer_2
  \_8_32寄存器组_1  \u_8_32寄存器组_1_1  (
    .W_En(and_2_out), .W_star(W_star[2:0]), .WD(WD), .R1_star(R1_star[2:0]), .R2_star(R2_star[2:0]),
    .R1_Out(\n8_32寄存器组_1_1_r1_out ), .R2_Out(\n8_32寄存器组_1_1_r2_out ), .Clk(Clk));
  and and_3 (and_3_out, W3, W_En);
  assign R2D = decoder_3_out1 ? \n8_32寄存器组_1_1_r2_out  : 32'bz;  // Controlled_Buffer controlled_buffer_3
  \_8_32寄存器组_1  \u_8_32寄存器组_1_2  (
    .W_En(and_3_out), .W_star(W_star[2:0]), .WD(WD), .R1_star(R1_star[2:0]), .R2_star(R2_star[2:0]),
    .R1_Out(\n8_32寄存器组_1_2_r1_out ), .R2_Out(\n8_32寄存器组_1_2_r2_out ), .Clk(Clk));
  assign R1D = decoder_2_out1 ? \n8_32寄存器组_1_1_r1_out  : 32'bz;  // Controlled_Buffer controlled_buffer_4
  and and_4 (and_4_out, W4, W_En);
  \_8_32寄存器组_1  \u_8_32寄存器组_1_3  (
    .W_En(and_4_out), .W_star(W_star[2:0]), .WD(WD), .R1_star(R1_star[2:0]), .R2_star(R2_star[2:0]),
    .R1_Out(\n8_32寄存器组_1_3_r1_out ), .R2_Out(\n8_32寄存器组_1_3_r2_out ), .Clk(Clk));
  assign R1D = decoder_2_out2 ? \n8_32寄存器组_1_2_r1_out  : 32'bz;  // Controlled_Buffer controlled_buffer_5
  assign R2D = decoder_3_out2 ? \n8_32寄存器组_1_2_r2_out  : 32'bz;  // Controlled_Buffer controlled_buffer_6
  assign R1D = decoder_2_out3 ? \n8_32寄存器组_1_3_r1_out  : 32'bz;  // Controlled_Buffer controlled_buffer_7
  assign R2D = decoder_3_out3 ? \n8_32寄存器组_1_3_r2_out  : 32'bz;  // Controlled_Buffer controlled_buffer_8

  // Other names for the same wires on the sheet: R1__3[2:0] = R1_star[2:0]; R2__3[2:0] = R2_star[2:0];
  //   W__3[2:0] = W_star[2:0]
endmodule

module \_8_32寄存器组_0  (
  input  W_En,
  input  [2:0] W_star,
  input  [31:0] WD,
  input  [2:0] R1_star,
  input  [2:0] R2_star,
  input  Clk,
  output [31:0] R1_Out,
  output [31:0] R2_Out
);

  wire _0, _1, _2, _3, _4, _5, _6, _7, and_1_out, and_2_out, and_3_out, and_4_out, and_5_out, and_6_out,
       and_7_out, and_8_out, not_1_out, not_2_out;
  wire [31:0] register_1_q, register_2_q, register_3_q, register_4_q, register_5_q, register_6_q,
       register_7_q, register_8_q;

  Decoder #(.select(3), .disabled(0)) decoder_1 (
    .out0(_0), .out1(_1), .out2(_2), .out3(_3), .out4(_4), .out5(_5), .out6(_6), .out7(_7), .sel(W_star),
    .en(W_En));
  Register #(.width(32), .trigger("falling")) register_1 (
    .Q(register_1_q), .clk(and_1_out), .clr(1'b1));  // open: D, en
  and and_1 (and_1_out, _0, Clk, W_En);
  Register #(.width(32), .trigger("falling")) register_2 (.D(WD), .Q(register_2_q), .clk(and_2_out));  // open: en, clr
  and and_2 (and_2_out, _4, Clk, W_En);
  Register #(.width(32), .trigger("falling")) register_3 (.D(WD), .Q(register_3_q), .clk(and_3_out));  // open: en, clr
  and and_3 (and_3_out, _1, Clk, W_En);
  Register #(.width(32), .trigger("falling")) register_4 (.D(WD), .Q(register_4_q), .clk(and_4_out));  // open: en, clr
  and and_4 (and_4_out, _5, Clk, W_En);
  Register #(.width(32), .trigger("falling")) register_5 (.D(WD), .Q(register_5_q), .clk(and_5_out));  // open: en, clr
  and and_5 (and_5_out, _2, Clk, W_En);
  Register #(.width(32), .trigger("falling")) register_6 (.D(WD), .Q(register_6_q), .clk(and_6_out));  // open: en, clr
  and and_6 (and_6_out, _6, Clk, W_En);
  Register #(.width(32), .trigger("falling")) register_7 (.D(WD), .Q(register_7_q), .clk(and_7_out));  // open: en, clr
  and and_7 (and_7_out, _3, Clk, W_En);
  Register #(.width(32), .trigger("falling")) register_8 (.D(WD), .Q(register_8_q), .clk(and_8_out));  // open: en, clr
  and and_8 (and_8_out, _7, Clk, W_En);
  not not_1 (not_1_out, R1_star[2]);
  Multiplexer #(.select(2), .width(32)) multiplexer_1 (
    .in0(register_1_q), .in1(register_3_q), .in2(register_5_q), .in3(register_7_q), .out(R1_Out),
    .sel(R1_star[1:0]), .en(not_1_out));
  Multiplexer #(.select(2), .width(32)) multiplexer_2 (
    .in0(register_1_q), .in1(register_3_q), .in2(register_5_q), .in3(register_7_q), .out(R2_Out),
    .sel(R2_star[1:0]), .en(not_2_out));
  Multiplexer #(.select(2), .width(32)) multiplexer_3 (
    .in0(register_2_q), .in1(register_4_q), .in2(register_6_q), .in3(register_8_q), .out(R1_Out),
    .sel(R1_star[1:0]), .en(R1_star[2]));
  Multiplexer #(.select(2), .width(32)) multiplexer_4 (
    .in0(register_2_q), .in1(register_4_q), .in2(register_6_q), .in3(register_8_q), .out(R2_Out),
    .sel(R2_star[1:0]), .en(R2_star[2]));
  not not_2 (not_2_out, R2_star[2]);

  // Other names for the same wires on the sheet: R1[2:0] = R1_star; R2[2:0] = R2_star; 写使能 = W_En

  // Notes on the sheet:
  //   3-8译码器
endmodule

module \_8_32寄存器组_1  (
  input  W_En,
  input  [2:0] W_star,
  input  [31:0] WD,
  input  [2:0] R1_star,
  input  [2:0] R2_star,
  input  Clk,
  output [31:0] R1_Out,
  output [31:0] R2_Out
);

  wire _0, _1, _2, _3, _4, _5, _6, _7, and_1_out, and_2_out, and_3_out, and_4_out, and_5_out, and_6_out,
       and_7_out, and_8_out, not_1_out, not_2_out;
  wire [31:0] register_1_q, register_2_q, register_3_q, register_4_q, register_5_q, register_6_q,
       register_7_q, register_8_q;

  Decoder #(.select(3), .disabled(0)) decoder_1 (
    .out0(_0), .out1(_1), .out2(_2), .out3(_3), .out4(_4), .out5(_5), .out6(_6), .out7(_7), .sel(W_star),
    .en(W_En));
  Register #(.width(32), .trigger("falling")) register_1 (.D(WD), .Q(register_1_q), .clk(and_1_out));  // open: en, clr
  and and_1 (and_1_out, _0, Clk, W_En);
  Register #(.width(32), .trigger("falling")) register_2 (.D(WD), .Q(register_2_q), .clk(and_2_out));  // open: en, clr
  and and_2 (and_2_out, _4, Clk, W_En);
  Register #(.width(32), .trigger("falling")) register_3 (.D(WD), .Q(register_3_q), .clk(and_3_out));  // open: en, clr
  and and_3 (and_3_out, _1, Clk, W_En);
  Register #(.width(32), .trigger("falling")) register_4 (.D(WD), .Q(register_4_q), .clk(and_4_out));  // open: en, clr
  and and_4 (and_4_out, _5, Clk, W_En);
  Register #(.width(32), .trigger("falling")) register_5 (.D(WD), .Q(register_5_q), .clk(and_5_out));  // open: en, clr
  and and_5 (and_5_out, _2, Clk, W_En);
  Register #(.width(32), .trigger("falling")) register_6 (.D(WD), .Q(register_6_q), .clk(and_6_out));  // open: en, clr
  and and_6 (and_6_out, _6, Clk, W_En);
  Register #(.width(32), .trigger("falling")) register_7 (.D(WD), .Q(register_7_q), .clk(and_7_out));  // open: en, clr
  and and_7 (and_7_out, _3, Clk, W_En);
  Register #(.width(32), .trigger("falling")) register_8 (.D(WD), .Q(register_8_q), .clk(and_8_out));  // open: en, clr
  and and_8 (and_8_out, _7, Clk, W_En);
  not not_1 (not_1_out, R1_star[2]);
  Multiplexer #(.select(2), .width(32)) multiplexer_1 (
    .in0(register_1_q), .in1(register_3_q), .in2(register_5_q), .in3(register_7_q), .out(R1_Out),
    .sel(R1_star[1:0]), .en(not_1_out));
  Multiplexer #(.select(2), .width(32)) multiplexer_2 (
    .in0(register_1_q), .in1(register_3_q), .in2(register_5_q), .in3(register_7_q), .out(R2_Out),
    .sel(R2_star[1:0]), .en(not_2_out));
  Multiplexer #(.select(2), .width(32)) multiplexer_3 (
    .in0(register_2_q), .in1(register_4_q), .in2(register_6_q), .in3(register_8_q), .out(R1_Out),
    .sel(R1_star[1:0]), .en(R1_star[2]));
  Multiplexer #(.select(2), .width(32)) multiplexer_4 (
    .in0(register_2_q), .in1(register_4_q), .in2(register_6_q), .in3(register_8_q), .out(R2_Out),
    .sel(R2_star[1:0]), .en(R2_star[2]));
  not not_2 (not_2_out, R2_star[2]);

  // Other names for the same wires on the sheet: R1[2:0] = R1_star; R2[2:0] = R2_star; 写使能 = W_En

  // Notes on the sheet:
  //   3-8译码器
endmodule

module \进行移位运算  (
  input  [5:0] IN,
  output \移位 
);

  wire and_1_out, and_2_out, and_4_out, and_5_out, or_1_out;

  and and_1 (and_1_out, ~IN[4], ~IN[5]);  // AND_Gate
  and and_2 (and_2_out, ~IN[0], ~IN[1], ~IN[2], IN[3]);  // AND_Gate
  and and_3 (\移位 , and_1_out, or_1_out);
  and and_4 (and_4_out, ~IN[0], IN[1], IN[2], ~IN[3]);  // AND_Gate
  or or_1 (or_1_out, and_2_out, and_4_out, and_5_out);
  and and_5 (and_5_out, IN[0], IN[1], IN[2], ~IN[3]);  // AND_Gate
endmodule

module \I非ALU指令  (
  input  \使能 ,
  input  [5:0] IN,
  output lw,
  output sw,
  output beq
);

  wire and_1_out, and_3_out, and_5_out;

  and and_1 (and_1_out, ~IN[0], ~IN[1], ~IN[2], ~IN[3], IN[4], ~IN[5]);  // AND_Gate
  and and_2 (lw, and_1_out, \使能 );
  and and_3 (and_3_out, IN[0], ~IN[1], ~IN[2], ~IN[3], IN[4], ~IN[5]);  // AND_Gate
  and and_4 (sw, and_3_out, \使能 );
  and and_5 (and_5_out, ~IN[0], ~IN[1], ~IN[2], ~IN[3], ~IN[4], IN[5]);  // AND_Gate
  and and_6 (beq, and_5_out, \使能 );
endmodule
